// Logisim project exp6-1b.circ as structural Verilog: 1 circuit, main circuit main
module main (
  input  [2:0] A_B_C,
  output F
);

  wire decoder_1_out0, decoder_1_out1, decoder_1_out6;

  Decoder #(.select(3), .tristate("false")) decoder_1 (
    .out0(decoder_1_out0), .out1(decoder_1_out1), .out6(decoder_1_out6), .sel(A_B_C));  // open: out2, out3, out4, out5, out7
  or or_1 (F, decoder_1_out0, decoder_1_out1, decoder_1_out6);

  // Notes on the sheet:
  //   Clinten Hopkins
  //   CSCI 250 - 03
  //   Experiment 06 - 1b
endmodule
