// Logisim project exp6-1c.circ as structural Verilog: 1 circuit, main circuit main
module main (
  input  [2:0] ABC,
  output F
);

  Multiplexer #(.select(3), .width(1)) multiplexer_1 (
    .in0(1'b1), .in1(1'b0), .in2(1'b0), .in3(1'b1), .in4(1'b1), .in5(1'b1), .in6(1'b0), .in7(1'b1), .out(F),
    .sel(ABC));

  // Notes on the sheet:
  //   PWR
  //   GRD
  //   Clinten Hopkins
  //   CSCI 250 - 03
  //   Experiment 06 - 1c
endmodule
