// Logisim project exp6-2c.circ as structural Verilog: 1 circuit, main circuit main
module main (
  input  DATA
);

  wire bcd_to_7_segment_decoder_1_p7, bcd_to_7_segment_decoder_1_p8, bcd_to_7_segment_decoder_1_p9,
       bcd_to_7_segment_decoder_1_p10, bcd_to_7_segment_decoder_1_p11, bcd_to_7_segment_decoder_1_p12,
       bcd_to_7_segment_decoder_1_p13, button_1_out, button_2_out, j_k_ff_1_q, j_k_ff_1_qn, j_k_ff_2_q,
       j_k_ff_2_qn, j_k_ff_3_q, j_k_ff_3_qn, j_k_ff_4_q, not_1_out;

  not not_1 (not_1_out, DATA);
  Button button_1 (.out(button_1_out));
  J_K_Flip_Flop #(.trigger("rising")) j_k_ff_1 (
    .J(DATA), .clk(button_1_out), .K(not_1_out), .Q(j_k_ff_1_q), .Qn(j_k_ff_1_qn), .reset(button_2_out));  // open: preset, en
  Button button_2 (.out(button_2_out));
  J_K_Flip_Flop #(.trigger("rising")) j_k_ff_2 (
    .J(j_k_ff_1_q), .clk(button_1_out), .K(j_k_ff_1_qn), .Q(j_k_ff_2_q), .Qn(j_k_ff_2_qn),
    .reset(button_2_out));  // open: preset, en
  J_K_Flip_Flop #(.trigger("rising")) j_k_ff_3 (
    .J(j_k_ff_2_q), .clk(button_1_out), .K(j_k_ff_2_qn), .Q(j_k_ff_3_q), .Qn(j_k_ff_3_qn),
    .reset(button_2_out));  // open: preset, en
  J_K_Flip_Flop #(.trigger("rising")) j_k_ff_4 (
    .J(j_k_ff_3_q), .clk(button_1_out), .K(j_k_ff_3_qn), .Q(j_k_ff_4_q), .reset(button_2_out));  // open: Qn, preset, en
  // BCD_to_7_segment_decoder bcd_to_7_segment_decoder_1: pin names not known; wires that end beside it: button_1_out, button_2_out, j_k_ff_4_q, j_k_ff_3_q, j_k_ff_2_q, j_k_ff_1_q, bcd_to_7_segment_decoder_1_p7, bcd_to_7_segment_decoder_1_p8, bcd_to_7_segment_decoder_1_p9, bcd_to_7_segment_decoder_1_p10, bcd_to_7_segment_decoder_1_p11, bcd_to_7_segment_decoder_1_p12, bcd_to_7_segment_decoder_1_p13
  _7_Segment_Display u_7_segment_display_1 (
    .g(bcd_to_7_segment_decoder_1_p13), .f(bcd_to_7_segment_decoder_1_p12),
    .a(bcd_to_7_segment_decoder_1_p7), .b(bcd_to_7_segment_decoder_1_p8), .e(bcd_to_7_segment_decoder_1_p11),
    .d(bcd_to_7_segment_decoder_1_p10), .c(bcd_to_7_segment_decoder_1_p9));  // open: dp

  // Notes on the sheet:
  //   CLK
  //   A
  //   CLR
  //   B
  //   C
  //   D
  //   Clinten Hopkins
  //   CSCI 250 - 03
  //   Experiment 06 -2c
endmodule
