// Logisim project exp7-1.circ as structural Verilog: 2 circuits, main circuit 1-bit ALU
module _1_bit_ALU (
  input  add_sub,
  input  C_in,
  input  [1:0] Selects,
  input  A,
  input  B,
  input  sli,
  output R,
  output C_out,
  output FA_out
);

  wire and_1_out, or_1_out, xor_1_out;

  xor xor_1 (xor_1_out, B, add_sub);
  and and_1 (and_1_out, A, B);
  or or_1 (or_1_out, A, B);
  Adder #(.width(1)) adder_1 (.a(A), .b(xor_1_out), .out(FA_out), .cin(C_in), .cout(C_out));
  Multiplexer #(.select(2), .width(1)) multiplexer_1 (
    .in0(and_1_out), .in1(or_1_out), .in2(FA_out), .in3(sli), .out(R), .sel(Selects));

  // Notes on the sheet:
  //   Name:
  //   Section #
  //   Experiment #
  //   Activity #
  //   Clinten Hopkins
  //   03
  //   07
  //   a
endmodule

module _4_bit_ALU (
  input  [3:0] A,
  input  [3:0] B,
  input  Add_Sub,
  input  [1:0] Select,
  output Zero,
  output [3:0] Result,
  output Overflow
);

  wire n1_bit_alu_1_c_out, n1_bit_alu_2_c_out, n1_bit_alu_3_c_out, n1_bit_alu_4_c_out, n1_bit_alu_4_fa_out;

  _1_bit_ALU u_1_bit_alu_1 (
    .A(A[0]), .B(B[0]), .sli(n1_bit_alu_4_fa_out), .add_sub(Add_Sub), .C_in(Add_Sub), .Selects(Select),
    .C_out(n1_bit_alu_1_c_out), .R(Result[0]));  // open: FA_out
  _1_bit_ALU u_1_bit_alu_2 (
    .A(A[1]), .B(B[1]), .sli(1'b0), .add_sub(Add_Sub), .C_in(n1_bit_alu_1_c_out), .Selects(Select),
    .C_out(n1_bit_alu_2_c_out), .R(Result[1]));  // open: FA_out
  _1_bit_ALU u_1_bit_alu_3 (
    .A(A[2]), .B(B[2]), .sli(1'b0), .add_sub(Add_Sub), .C_in(n1_bit_alu_2_c_out), .Selects(Select),
    .C_out(n1_bit_alu_3_c_out), .R(Result[2]));  // open: FA_out
  _1_bit_ALU u_1_bit_alu_4 (
    .A(A[3]), .B(B[3]), .sli(1'b0), .add_sub(Add_Sub), .C_in(n1_bit_alu_3_c_out), .Selects(Select),
    .C_out(n1_bit_alu_4_c_out), .FA_out(n1_bit_alu_4_fa_out), .R(Result[3]));
  xor xor_1 (Overflow, n1_bit_alu_3_c_out, n1_bit_alu_4_c_out);
  nor nor_1 (Zero, Result[0], Result[1], Result[2], Result[3]);

  // Notes on the sheet:
  //   GND
  //   Name:
  //   Section #
  //   Experiment #
  //   Activity #
  //   03
  //   07
  //   b
  //   Clinten Hopkins
endmodule
